// Logisim project 816906-BR32test.circ as structural Verilog: 3 circuits, main circuit main
module BR4 (
  input  Reloj,
  input  [1:0] RA,
  input  [1:0] RB,
  input  RegWr,
  input  [1:0] RW,
  input  Reset,
  input  [31:0] busW,
  output [31:0] busA,
  output [31:0] busB
);

  wire decoder_1_out0, decoder_1_out1, decoder_1_out2, decoder_1_out3;
  wire [31:0] register_1_q, register_2_q, register_3_q, register_4_q;

  Decoder #(.select(2), .disabled(0)) decoder_1 (
    .out0(decoder_1_out0), .out1(decoder_1_out1), .out2(decoder_1_out2), .out3(decoder_1_out3), .sel(RW),
    .en(RegWr));
  Register #(.width(32)) register_1 (.D(busW), .en(decoder_1_out0), .Q(register_1_q), .clk(Reloj), .clr(Reset));
  Register #(.width(32)) register_2 (.D(busW), .en(decoder_1_out1), .Q(register_2_q), .clk(Reloj), .clr(Reset));
  Register #(.width(32)) register_3 (.D(busW), .en(decoder_1_out2), .Q(register_3_q), .clk(Reloj), .clr(Reset));
  Register #(.width(32)) register_4 (.D(busW), .en(decoder_1_out3), .Q(register_4_q), .clk(Reloj), .clr(Reset));
  // Probe on busA
  Multiplexer #(.select(2), .width(32), .enable("false")) multiplexer_1 (
    .in0(register_1_q), .in1(register_2_q), .in2(register_3_q), .in3(register_4_q), .out(busA), .sel(RA));
  Multiplexer #(.select(2), .width(32), .enable("false")) multiplexer_2 (
    .in0(register_1_q), .in1(register_2_q), .in2(register_3_q), .in3(register_4_q), .out(busB), .sel(RB));
  // Probe on busB
endmodule

module BR32 (
  input  Reset,
  input  Reloj,
  input  [4:0] RA,
  input  [4:0] RB,
  input  RegWr,
  input  [4:0] RW,
  input  [31:0] busW,
  output [31:0] busA,
  output [31:0] busB
);

  wire decoder_1_out0, decoder_1_out1, decoder_1_out2, decoder_1_out3, decoder_1_out4, decoder_1_out5,
       decoder_1_out6, decoder_1_out7;
  wire [31:0] br4_1_busa, br4_1_busb, br4_2_busa, br4_2_busb, br4_3_busa, br4_3_busb, br4_4_busa, br4_4_busb,
       br4_5_busa, br4_5_busb, br4_6_busa, br4_6_busb, br4_7_busa, br4_7_busb, br4_8_busa, br4_8_busb;

  Decoder #(.select(3), .disabled(0)) decoder_1 (
    .out0(decoder_1_out0), .out1(decoder_1_out1), .out2(decoder_1_out2), .out3(decoder_1_out3),
    .out4(decoder_1_out4), .out5(decoder_1_out5), .out6(decoder_1_out6), .out7(decoder_1_out7),
    .sel(RW[4:2]), .en(RegWr));
  BR4 br4_1 (
    .RA(RA[1:0]), .RB(RB[1:0]), .RW(RW[1:0]), .busW(busW), .Reloj(Reloj), .RegWr(decoder_1_out0),
    .Reset(Reset), .busA(br4_1_busa), .busB(br4_1_busb));
  BR4 br4_2 (
    .RA(RA[1:0]), .RB(RB[1:0]), .RW(RW[1:0]), .busW(busW), .Reloj(Reloj), .RegWr(decoder_1_out1),
    .Reset(Reset), .busA(br4_2_busa), .busB(br4_2_busb));
  BR4 br4_3 (
    .RA(RA[1:0]), .RB(RB[1:0]), .RW(RW[1:0]), .busW(busW), .Reloj(Reloj), .RegWr(decoder_1_out2),
    .Reset(Reset), .busA(br4_3_busa), .busB(br4_3_busb));
  BR4 br4_4 (
    .RA(RA[1:0]), .RB(RB[1:0]), .RW(RW[1:0]), .busW(busW), .Reloj(Reloj), .RegWr(decoder_1_out3),
    .Reset(Reset), .busA(br4_4_busa), .busB(br4_4_busb));
  BR4 br4_5 (
    .RA(RA[1:0]), .RB(RB[1:0]), .RW(RW[1:0]), .busW(busW), .Reloj(Reloj), .RegWr(decoder_1_out4),
    .Reset(Reset), .busA(br4_5_busa), .busB(br4_5_busb));
  BR4 br4_6 (
    .RA(RA[1:0]), .RB(RB[1:0]), .RW(RW[1:0]), .busW(busW), .Reloj(Reloj), .RegWr(decoder_1_out5),
    .Reset(Reset), .busA(br4_6_busa), .busB(br4_6_busb));
  BR4 br4_7 (
    .RA(RA[1:0]), .RB(RB[1:0]), .RW(RW[1:0]), .busW(busW), .Reloj(Reloj), .RegWr(decoder_1_out6),
    .Reset(Reset), .busA(br4_7_busa), .busB(br4_7_busb));
  BR4 br4_8 (
    .RA(RA[1:0]), .RB(RB[1:0]), .RW(RW[1:0]), .busW(busW), .Reloj(Reloj), .RegWr(decoder_1_out7),
    .Reset(Reset), .busA(br4_8_busa), .busB(br4_8_busb));
  // Probe on busA
  Multiplexer #(.select(3), .width(32), .disabled(0), .enable("false")) multiplexer_1 (
    .in0(br4_1_busa), .in1(br4_2_busa), .in2(br4_3_busa), .in3(br4_4_busa), .in4(br4_5_busa),
    .in5(br4_6_busa), .in6(br4_7_busa), .in7(br4_8_busa), .out(busA), .sel(RA[4:2]));
  Multiplexer #(.select(3), .width(32), .disabled(0), .enable("false")) multiplexer_2 (
    .in0(br4_1_busb), .in1(br4_2_busb), .in2(br4_3_busb), .in3(br4_4_busb), .in4(br4_5_busb),
    .in5(br4_6_busb), .in6(br4_7_busb), .in7(br4_8_busb), .out(busB), .sel(RB[4:2]));
  // Probe on busB

  // Other names for the same wires on the sheet: RA_t[2:0] = RA[4:2]; RB_t[2:0] = RB[4:2]
endmodule

module main (
  input  Reset
);

  wire br32test_1_p5, br32test_1_p7, br32test_1_p9, br32test_1_p11, clock_1_out;
  wire [4:0] br32test_1_p10, RA, RB;
  wire [31:0] br32test_1_p12, busA, busB;

  Clock clock_1 (.out(clock_1_out));
  // Probe on br32test_1_p5
  // Probe on br32test_1_p7
  // Probe on br32test_1_p9
  // BR32test br32test_1: pin names not known; wires that end beside it: RA, busA, RB, busB, br32test_1_p5, clock_1_out, br32test_1_p7, Reset, br32test_1_p9, br32test_1_p10, br32test_1_p11, br32test_1_p12
  BR32 br32_1 (
    .RA(RA), .RB(RB), .RW(br32test_1_p10), .busW(br32test_1_p12), .Reset(Reset), .Reloj(clock_1_out),
    .RegWr(br32test_1_p11), .busA(busA), .busB(busB));
endmodule
